# Fritzing sketch Attiny Intermediate breadboard (saved by Fritzing 0.9.2b)
breadboards: 1

parts:
  U4 = DIODE-ZENER [package=diode-zener]
  R10 = Resistor [tolerance=±5% resistance=10k package="0603 [SMD]"]
  U6 = DIODE-ZENER [package=diode-zener]
  C2 = Electrolytic Capacitor [capacitance=100µF package="200 mil [THT, electrolytic]"]
  R11 = Resistor [tolerance=±5% resistance=1k package="0603 [SMD]"]
  S3 = Reed switch [package=THT]
  U1 = ATTINY45 [package=dip]
  U2 = Voltage Regulator - 5V [package="DPak [SMD]"]
  R12 = Resistor [tolerance=±5% resistance=1.5k package=THT]
  IC1 = L293D [package=THT]
  Power_plug1 = Power plug  # not connected
  Q2 = TRANSISTOR_NPN [package=to-92-ammo]
  R8 = Resistor [tolerance=±5% resistance=10k package="0603 [SMD]"]
  Part1 = Arduino Uno (Rev3)  # not connected
  C3 = Electrolytic Capacitor [capacitance=100µF package="200 mil [THT, electrolytic]"]
  R9 = Resistor [tolerance=±5% resistance=1k package="0603 [SMD]"]
  Q3 = TRANSISTOR_NPN [package=to-92-ammo]
  TRRS1 = Audio Jack (TRRS) 3.5mm [part_number="LUMBERG JEITA RC-5325A" package="RC-5325A [SMD]"]
  M1 = Stepper Motor - Bipolar

nets:
  N1: U4.C, TRRS1.RING2
  N2: R10.Pin_0, U2.output_voltage, R12.Pin_0, IC1.Enable_1, IC1.Enable_2, IC1.+V, R8.Pin_0, C3.+
  N3: R10.Pin_1, U1.PB4(ADC2), IC1.In_1, R9.Pin_0
  N4: U6.C, TRRS1.SLEEVE
  GND: C2.+, U1.GND, U2.GND, IC1.0V, Q2.E, C3.-, Q3.E, TRRS1.RING1
  N5: R11.Pin_0, IC1.In_4
  N6: R11.Pin_1, Q3.B
  N7: S3.pin_1, U1.PB3(ADC3)
  N8: S3.pin_2, R12.Pin_1
  N9: U2.input_voltage, IC1.+Vmotor, TRRS1.TIP
  N10: IC1.Out_1_(_Controlled_by_Enable_1_), M1.B
  N11: IC1.Out_2_(_Controlled_by_Enable_1_), M1.D
  N12: IC1.In_2, Q2.C
  N13: IC1.In_3, R8.Pin_1, Q3.C
  N14: IC1.Out_3_(_Controlled_by_Enable_2_), M1.A
  N15: IC1.Out_4_(_Controlled_by_Enable_2_), M1.C
  N16: Q2.B, R9.Pin_1

notes:
  Reed sensor
  (magnet X positioning)
  Attiny Intermediate
