# Fritzing sketch Attiny Stepper (I2C) breadboard (saved by Fritzing 0.9.2b)
breadboards: 1

parts:
  IC1 = L293D [package=THT]
  U1 = ATTINY45 [package=dip]
  M1 = Stepper Motor - Bipolar
  U2 = Voltage Regulator - 5V [package="DPak [SMD]"]
  Q1 = TRANSISTOR_NPN [package=to-92]
  U3 = POT [package=pot_mammoth]
  C3 = Electrolytic Capacitor [capacitance=100µF package="200 mil [THT, electrolytic]"]
  Part1 = Arduino Uno (Rev3)  # not connected
  TRRS1 = Audio Jack (TRRS) 3.5mm [part_number="LUMBERG JEITA RC-5325A" package="RC-5325A [SMD]"]
  U4 = DIODE-ZENER [package=diode-zener]
  R3 = Resistor [tolerance=±5% resistance=4.7k package=THT]
  C2 = Electrolytic Capacitor [capacitance=100µF package="200 mil [THT, electrolytic]"]
  R6 = Resistor [tolerance=±5% resistance=4.7k package=THT]
  U6 = DIODE-ZENER [package=diode-zener]
  L1 = Solenoid
  R7 = Resistor [tolerance=±5% resistance=100 package=THT]
  Power_plug1 = Power plug  # not connected
  Q2 = TRANSISTOR_NPN [package=to-92-ammo]
  Q3 = TRANSISTOR_NPN [package=to-92-ammo]
  R8 = Resistor [tolerance=±5% resistance=10k package="0603 [SMD]"]
  R9 = Resistor [tolerance=±5% resistance=1k package="0603 [SMD]"]
  R10 = Resistor [tolerance=±5% resistance=10k package="0603 [SMD]"]
  R11 = Resistor [tolerance=±5% resistance=1k package="0603 [SMD]"]

nets:
  N1: IC1.Enable_1, IC1.Enable_2, IC1.+V, U2.output_voltage, U3.E, C3.+, R3.Pin_0, R6.Pin_0, R8.Pin_0, R10.Pin_0
  N2: IC1.In_1, U1.PB4(ADC2), R9.Pin_0, R10.Pin_1
  N3: IC1.Out_1_(_Controlled_by_Enable_1_), M1.B
  GND: IC1.0V, U1.GND, U2.GND, Q1.E, C3.-, TRRS1.RING1, C2.-, Q2.E, Q3.E
  N4: IC1.Out_2_(_Controlled_by_Enable_1_), M1.D
  N5: IC1.In_2, Q2.C
  N6: IC1.+Vmotor, U2.input_voltage, TRRS1.TIP, C2.+
  N7: IC1.In_3, Q3.C, R8.Pin_1
  N8: IC1.Out_3_(_Controlled_by_Enable_2_), M1.A
  N9: IC1.Out_4_(_Controlled_by_Enable_2_), M1.C
  N10: IC1.In_4, R11.Pin_0
  N11: U1.PB5(NRES), R7.Pin_1
  N12: U1.PB3(ADC3), U3.A
  N13: Q1.B, R7.Pin_0
  N14: Q1.C, L1.pin1
  N15: TRRS1.SLEEVE, R6.Pin_1, U6.C
  N16: TRRS1.RING2, U4.C
  N17: Q2.B, R9.Pin_1
  N18: Q3.B, R11.Pin_1

notes:
  Variable resistor
  (worm gear 20:1)
  Solenoid stopper
  (pin 5 - disable Reset)
  I2c METHOD
