# Fritzing sketch ATmega328P Internal breadboard (saved by Fritzing 0.9.2b)
breadboards: 1

parts:
  IC1 = L293D [package=THT]
  M1 = Stepper Motor - Bipolar
  U2 = Voltage Regulator - 5V [package="DPak [SMD]"]
  C3 = Electrolytic Capacitor [capacitance=100µF package="200 mil [THT, electrolytic]"]
  TRRS1 = Audio Jack (TRRS) 3.5mm [part_number="LUMBERG JEITA RC-5325A" package="RC-5325A [SMD]"]
  U4 = DIODE-ZENER [package=diode-zener]
  C2 = Electrolytic Capacitor [capacitance=100µF package="200 mil [THT, electrolytic]"]
  U6 = DIODE-ZENER [package=diode-zener]
  Power_plug1 = Power plug  # not connected
  U7 = atmega328 [package=dip]
  Q1 = TRANSISTOR_NPN [package=to-92]
  R1 = Resistor [tolerance=±5% resistance=1.5k package="1206 [SMD]"]
  LED1 = LEDs [package=led10mm]
  S4 = Reed switch [package=THT]
  R15 = Resistor [tolerance=±5% resistance=10k package=THT]
  R16 = Resistor [tolerance=±5% resistance=10k package=THT]  # not connected
  U8 = ESP8266 WiFi Module [part_number=ESP8266]
  D4 = Diode [package=diode-1n4001]  # not connected
  D5 = Diode [package=diode-1n4001]
  M2 = Stepper Motor - Bipolar
  J1 = AVR ISP 6 Pin [package=2x3_lock]
  S5 = Pushbutton [package=THT]
  R17 = Resistor [tolerance=±5% resistance=10k package=THT]

nets:
  N1: IC1.Enable_1, IC1.+Vmotor, IC1.Enable_2, IC1.+V, U2.output_voltage, C3.+, U7.VCC, U7.AVCC, R15.Pin_0, D5.A, J1.2, S5.leg0
  N2: IC1.In_1, U7.D4
  N3: IC1.Out_1_(_Controlled_by_Enable_1_), M1.B
  GND: IC1.0V, U2.GND, C3.-, TRRS1.TIP, TRRS1.RING1, C2.-, U7.GND, Q1.E, LED1.A, U8.GND, J1.6, R17.Pin_1
  N4: IC1.Out_2_(_Controlled_by_Enable_1_), M1.D
  N5: IC1.In_2, U7.D3_(PWM)
  N6: IC1.In_3, U7.A3
  N7: IC1.Out_3_(_Controlled_by_Enable_2_), M1.C
  N8: IC1.Out_4_(_Controlled_by_Enable_2_), M1.A
  N9: IC1.In_4, U7.D2
  N10: U2.input_voltage, C2.+
  N11: TRRS1.SLEEVE, U6.C, U7.A5
  N12: TRRS1.RING2, U4.C, U7.A4
  N13: U7.RESET, J1.5
  N14: U7.D0_(RX), U8.TXD
  N15: U7.D1_(TX), U8.RXD, U8.GPIO_0
  N16: U7.D5_(PWM), M2.D
  N17: U7.D6_(PWM), M2.B
  N18: U7.D7, M2.C
  N19: U7.D8, M2.A
  N20: U7.D9_(PWM), R1.Pin_1
  N21: U7.D10_(PWM), S5.leg1, R17.Pin_0
  N22: U7.D11_(PWM), J1.4
  N23: U7.D12, J1.1
  N24: U7.D13, J1.3
  N25: U7.A2, S4.pin_1
  N26: Q1.B, R1.Pin_0
  N27: Q1.C, LED1.C
  N28: S4.pin_2, R15.Pin_1
  N29: U8.VCC, U8.RST, U8.CH_PD

notes:
  ESP8266-01 as web interface
  Lamp 12v
  (dimmer circuit)
  Reed sensor NO
  (magnet Y positioning)
  Micro Stepper slider
  ...smaller
  Mini Stepper Y
  Button NO (to detect slider reaching end)
  ISP header

custom parts:
  ESP8266 WiFi Module: Generic WiFi Module based on the ESP8266 with onboard PCB antenna and UART communications
